// Logisim project Tennis.circ as structural Verilog: 8 circuits, main circuit main
module main (
);

  wire clock_1_out;
  wire [4:0] joystick_1_y, kinematiccontroller_1_ballx, kinematiccontroller_1_bally,
       kinematiccontroller_1_chipid, kinematiccontroller_1_leftbaty, kinematiccontroller_1_rightbaty,
       not_1_out, undriven, videosection_1_ballx_2, videosection_1_bally_2, videosection_1_chipid_2,
       videosection_1_leftbaty_2, videosection_1_rightbaty_2, videosection_2_ballx_2, videosection_2_bally_2,
       videosection_2_chipid_2, videosection_2_leftbaty_2, videosection_2_rightbaty_2,
       videosection_3_ballx_2, videosection_3_bally_2, videosection_3_chipid_2, videosection_3_leftbaty_2,
       videosection_3_rightbaty_2;
  wire [31:0] videosection_1__0, videosection_1_out_7, videosection_1_out_8, videosection_1_out_9,
       videosection_1_out_10, videosection_1_out_11, videosection_1_out_12, videosection_1_out_13,
       videosection_2__0, videosection_2_out_7, videosection_2_out_8, videosection_2_out_9,
       videosection_2_out_10, videosection_2_out_11, videosection_2_out_12, videosection_2_out_13,
       videosection_3__0, videosection_3_out_7, videosection_3_out_8, videosection_3_out_9,
       videosection_3_out_10, videosection_3_out_11, videosection_3_out_12, videosection_3_out_13,
       videosection_4__0, videosection_4_out_7, videosection_4_out_8, videosection_4_out_9,
       videosection_4_out_10, videosection_4_out_11, videosection_4_out_12, videosection_4_out_13;

  Hex_Digit_Display hex_digit_display_1 ();  // open: value, dp
  Hex_Digit_Display hex_digit_display_2 ();  // open: value, dp
  Joystick #(.bits(5)) joystick_1 (.y(joystick_1_y));  // open: x
  // Probe on joystick_1_y
  assign not_1_out = ~joystick_1_y;  // NOT_Gate not_1, 5 bits wide
  // Probe on not_1_out
  DotMatrix #(.matrixcols(32), .matrixrows(32)) dotmatrix_1 (
    .col0(videosection_1__0), .col1(videosection_1_out_7), .col2(videosection_1_out_8),
    .col3(videosection_1_out_9), .col4(videosection_1_out_10), .col5(videosection_1_out_11),
    .col6(videosection_1_out_12), .col7(videosection_1_out_13), .col8(videosection_2__0),
    .col9(videosection_2_out_7), .col10(videosection_2_out_8), .col11(videosection_2_out_9),
    .col12(videosection_2_out_10), .col13(videosection_2_out_11), .col14(videosection_2_out_12),
    .col15(videosection_2_out_13), .col16(videosection_3__0), .col17(videosection_3_out_7),
    .col18(videosection_3_out_8), .col19(videosection_3_out_9), .col20(videosection_3_out_10),
    .col21(videosection_3_out_11), .col22(videosection_3_out_12), .col23(videosection_3_out_13),
    .col24(videosection_4__0), .col25(videosection_4_out_7), .col26(videosection_4_out_8),
    .col27(videosection_4_out_9), .col28(videosection_4_out_10), .col29(videosection_4_out_11),
    .col30(videosection_4_out_12), .col31(videosection_4_out_13));
  kinematicController kinematiccontroller_1 (
    .chipId(kinematiccontroller_1_chipid), .ballX(kinematiccontroller_1_ballx),
    .ballY(kinematiccontroller_1_bally), .leftBatY(kinematiccontroller_1_leftbaty),
    .rightBatY(kinematiccontroller_1_rightbaty), .Joystick(not_1_out), .Clock(clock_1_out),
    .rightBatPositionIn(undriven));
  videoSection videosection_1 (
    .chipId(kinematiccontroller_1_chipid), .ballX(kinematiccontroller_1_ballx),
    .ballY(kinematiccontroller_1_bally), .leftBatY(kinematiccontroller_1_leftbaty),
    .rightBatY(kinematiccontroller_1_rightbaty), .chipId_2(videosection_1_chipid_2),
    .ballX_2(videosection_1_ballx_2), .ballY_2(videosection_1_bally_2),
    .leftBatY_2(videosection_1_leftbaty_2), .rightBatY_2(videosection_1_rightbaty_2), ._0(videosection_1__0),
    .out_7(videosection_1_out_7), .out_8(videosection_1_out_8), .out_9(videosection_1_out_9),
    .out_10(videosection_1_out_10), .out_11(videosection_1_out_11), .out_12(videosection_1_out_12),
    .out_13(videosection_1_out_13));
  Clock clock_1 (.out(clock_1_out));
  videoSection videosection_2 (
    .chipId(videosection_1_chipid_2), .ballX(videosection_1_ballx_2), .ballY(videosection_1_bally_2),
    .leftBatY(videosection_1_leftbaty_2), .rightBatY(videosection_1_rightbaty_2),
    .chipId_2(videosection_2_chipid_2), .ballX_2(videosection_2_ballx_2), .ballY_2(videosection_2_bally_2),
    .leftBatY_2(videosection_2_leftbaty_2), .rightBatY_2(videosection_2_rightbaty_2), ._0(videosection_2__0),
    .out_7(videosection_2_out_7), .out_8(videosection_2_out_8), .out_9(videosection_2_out_9),
    .out_10(videosection_2_out_10), .out_11(videosection_2_out_11), .out_12(videosection_2_out_12),
    .out_13(videosection_2_out_13));
  videoSection videosection_3 (
    .chipId(videosection_2_chipid_2), .ballX(videosection_2_ballx_2), .ballY(videosection_2_bally_2),
    .leftBatY(videosection_2_leftbaty_2), .rightBatY(videosection_2_rightbaty_2),
    .chipId_2(videosection_3_chipid_2), .ballX_2(videosection_3_ballx_2), .ballY_2(videosection_3_bally_2),
    .leftBatY_2(videosection_3_leftbaty_2), .rightBatY_2(videosection_3_rightbaty_2), ._0(videosection_3__0),
    .out_7(videosection_3_out_7), .out_8(videosection_3_out_8), .out_9(videosection_3_out_9),
    .out_10(videosection_3_out_10), .out_11(videosection_3_out_11), .out_12(videosection_3_out_12),
    .out_13(videosection_3_out_13));
  videoSection videosection_4 (
    .chipId(videosection_3_chipid_2), .ballX(videosection_3_ballx_2), .ballY(videosection_3_bally_2),
    .leftBatY(videosection_3_leftbaty_2), .rightBatY(videosection_3_rightbaty_2), ._0(videosection_4__0),
    .out_7(videosection_4_out_7), .out_8(videosection_4_out_8), .out_9(videosection_4_out_9),
    .out_10(videosection_4_out_10), .out_11(videosection_4_out_11), .out_12(videosection_4_out_12),
    .out_13(videosection_4_out_13));  // open: chipId_2, ballX_2, ballY_2, leftBatY_2, rightBatY_2
  Hex_Digit_Display hex_digit_display_3 ();  // open: value, dp
  Hex_Digit_Display hex_digit_display_4 ();  // open: value, dp
endmodule

module VideoChip (
  input  [4:0] chipId,
  input  [4:0] ballX,
  input  [4:0] ballY,
  input  [4:0] leftBatY,
  input  [4:0] rightBatY,
  output [31:0] bitPattern,
  output [4:0] chipId_2,
  output [4:0] ballX_2,
  output [4:0] ballY_2,
  output [4:0] leftBatY_2,
  output [4:0] rightBatY_2
);

  wire comparator_1_eq, comparator_2_eq, comparator_3_eq, or_1_out;
  wire [31:0] ballvideo_1_out, chip_1_out_2, rightBatY_t;

  chip chip_1 (.in_1(leftBatY), .out_2(chip_1_out_2));
  Comparator #(.width(5), .mode("unsigned")) comparator_1 (
    .a(chipId), .b(5'b00011), .eq(comparator_1_eq));  // open: gt, lt
  Comparator #(.width(5), .mode("unsigned")) comparator_2 (
    .a(chipId), .b(5'b11100), .eq(comparator_2_eq));  // open: gt, lt
  Comparator #(.width(5), .mode("unsigned")) comparator_3 (
    .a(chipId), .b(ballX), .eq(comparator_3_eq));  // open: gt, lt
  ballVideo ballvideo_1 (.in(ballY), .out(ballvideo_1_out));
  Multiplexer #(.width(32)) multiplexer_1 (
    .in1(chip_1_out_2), .out(bitPattern), .sel(comparator_1_eq));  // open: in0, en
  or or_1 (or_1_out, comparator_1_eq, comparator_2_eq, comparator_3_eq);
  Multiplexer #(.width(32)) multiplexer_2 (
    .in1(ballvideo_1_out), .out(bitPattern), .sel(comparator_3_eq));  // open: in0, en
  chip chip_2 (.in_1(rightBatY), .out_2(rightBatY_t));
  Multiplexer #(.width(32)) multiplexer_3 (.in0({32{1'b0}}), .out(bitPattern), .sel(or_1_out));  // open: in1, en
  Multiplexer #(.width(32)) multiplexer_4 (
    .in1(rightBatY_t), .out(bitPattern), .sel(comparator_2_eq));  // open: in0, en
  inc inc_1 (.X(chipId), .R(chipId_2));  // open: Cout

  assign ballX_2 = ballX;
  assign ballY_2 = ballY;
  assign leftBatY_2 = leftBatY;
  assign rightBatY_2 = rightBatY;
endmodule

module videoSection (
  input  [4:0] chipId,
  input  [4:0] ballX,
  input  [4:0] ballY,
  input  [4:0] leftBatY,
  input  [4:0] rightBatY,
  output [31:0] _0,
  output [31:0] out_7,
  output [31:0] out_8,
  output [31:0] out_9,
  output [31:0] out_10,
  output [31:0] out_11,
  output [31:0] out_12,
  output [31:0] out_13,
  output [4:0] chipId_2,
  output [4:0] ballX_2,
  output [4:0] ballY_2,
  output [4:0] leftBatY_2,
  output [4:0] rightBatY_2
);

  wire [4:0] videochip_1_ballx_2, videochip_1_bally_2, videochip_1_chipid_2, videochip_1_leftbaty_2,
       videochip_1_rightbaty_2, videochip_2_ballx_2, videochip_2_bally_2, videochip_2_chipid_2,
       videochip_2_leftbaty_2, videochip_2_rightbaty_2, videochip_3_ballx_2, videochip_3_bally_2,
       videochip_3_chipid_2, videochip_3_leftbaty_2, videochip_3_rightbaty_2, videochip_4_ballx_2,
       videochip_4_bally_2, videochip_4_chipid_2, videochip_4_leftbaty_2, videochip_4_rightbaty_2,
       videochip_5_ballx_2, videochip_5_bally_2, videochip_5_chipid_2, videochip_5_leftbaty_2,
       videochip_5_rightbaty_2, videochip_6_ballx_2, videochip_6_bally_2, videochip_6_chipid_2,
       videochip_6_leftbaty_2, videochip_6_rightbaty_2, videochip_8_ballx_2, videochip_8_bally_2,
       videochip_8_chipid_2, videochip_8_leftbaty_2, videochip_8_rightbaty_2;

  VideoChip videochip_1 (
    .chipId(chipId), .ballX(ballX), .ballY(ballY), .leftBatY(leftBatY), .rightBatY(rightBatY),
    .bitPattern(_0), .chipId_2(videochip_1_chipid_2), .ballX_2(videochip_1_ballx_2),
    .ballY_2(videochip_1_bally_2), .leftBatY_2(videochip_1_leftbaty_2), .rightBatY_2(videochip_1_rightbaty_2));
  VideoChip videochip_2 (
    .chipId(videochip_1_chipid_2), .ballX(videochip_1_ballx_2), .ballY(videochip_1_bally_2),
    .leftBatY(videochip_1_leftbaty_2), .rightBatY(videochip_1_rightbaty_2), .bitPattern(out_7),
    .chipId_2(videochip_2_chipid_2), .ballX_2(videochip_2_ballx_2), .ballY_2(videochip_2_bally_2),
    .leftBatY_2(videochip_2_leftbaty_2), .rightBatY_2(videochip_2_rightbaty_2));
  VideoChip videochip_3 (
    .chipId(videochip_2_chipid_2), .ballX(videochip_2_ballx_2), .ballY(videochip_2_bally_2),
    .leftBatY(videochip_2_leftbaty_2), .rightBatY(videochip_2_rightbaty_2), .bitPattern(out_8),
    .chipId_2(videochip_3_chipid_2), .ballX_2(videochip_3_ballx_2), .ballY_2(videochip_3_bally_2),
    .leftBatY_2(videochip_3_leftbaty_2), .rightBatY_2(videochip_3_rightbaty_2));
  VideoChip videochip_4 (
    .chipId(videochip_3_chipid_2), .ballX(videochip_3_ballx_2), .ballY(videochip_3_bally_2),
    .leftBatY(videochip_3_leftbaty_2), .rightBatY(videochip_3_rightbaty_2), .bitPattern(out_9),
    .chipId_2(videochip_4_chipid_2), .ballX_2(videochip_4_ballx_2), .ballY_2(videochip_4_bally_2),
    .leftBatY_2(videochip_4_leftbaty_2), .rightBatY_2(videochip_4_rightbaty_2));
  VideoChip videochip_5 (
    .chipId(videochip_6_chipid_2), .ballX(videochip_6_ballx_2), .ballY(videochip_6_bally_2),
    .leftBatY(videochip_6_leftbaty_2), .rightBatY(videochip_6_rightbaty_2), .bitPattern(out_11),
    .chipId_2(videochip_5_chipid_2), .ballX_2(videochip_5_ballx_2), .ballY_2(videochip_5_bally_2),
    .leftBatY_2(videochip_5_leftbaty_2), .rightBatY_2(videochip_5_rightbaty_2));
  VideoChip videochip_6 (
    .chipId(videochip_4_chipid_2), .ballX(videochip_4_ballx_2), .ballY(videochip_4_bally_2),
    .leftBatY(videochip_4_leftbaty_2), .rightBatY(videochip_4_rightbaty_2), .bitPattern(out_10),
    .chipId_2(videochip_6_chipid_2), .ballX_2(videochip_6_ballx_2), .ballY_2(videochip_6_bally_2),
    .leftBatY_2(videochip_6_leftbaty_2), .rightBatY_2(videochip_6_rightbaty_2));
  VideoChip videochip_7 (
    .chipId(videochip_8_chipid_2), .ballX(videochip_8_ballx_2), .ballY(videochip_8_bally_2),
    .leftBatY(videochip_8_leftbaty_2), .rightBatY(videochip_8_rightbaty_2), .bitPattern(out_13),
    .chipId_2(chipId_2), .ballX_2(ballX_2), .ballY_2(ballY_2), .leftBatY_2(leftBatY_2),
    .rightBatY_2(rightBatY_2));
  VideoChip videochip_8 (
    .chipId(videochip_5_chipid_2), .ballX(videochip_5_ballx_2), .ballY(videochip_5_bally_2),
    .leftBatY(videochip_5_leftbaty_2), .rightBatY(videochip_5_rightbaty_2), .bitPattern(out_12),
    .chipId_2(videochip_8_chipid_2), .ballX_2(videochip_8_ballx_2), .ballY_2(videochip_8_bally_2),
    .leftBatY_2(videochip_8_leftbaty_2), .rightBatY_2(videochip_8_rightbaty_2));
endmodule

module kinematicController (
  input  [4:0] Joystick,
  input  [4:0] rightBatPositionIn,
  input  Clock,
  output [4:0] chipId,
  output [4:0] ballX,
  output [4:0] ballY,
  output [4:0] leftBatY,
  output [4:0] rightBatY
);

  wire comparator_1_lt;
  wire [7:0] ballX_q, undriven;

  Counter scoreLeft ();  // open: load, D, count, Q, carry, clk, clr
  Register #(.width(5)) componentX ();  // open: D, en, Q, clk, clr
  Register u_ballY ();  // open: D, en, Q, clk, clr
  Register #(.width(5)) componentY ();  // open: D, en, Q, clk, clr
  Register u_ballX (.D(undriven), .Q(ballX_q));  // open: en, clk, clr
  Counter counter_1 ();  // open: load, D, count, Q, carry, clk, clr
  Comparator #(.width(5), .mode("unsigned")) comparator_1 (
    .a(ballX_q[4:0]), .b(5'b01110), .lt(comparator_1_lt));  // open: gt, eq
  Register #(.width(5)) rightBatPosition (
    .D(rightBatPositionIn), .en(comparator_1_lt), .Q(rightBatY));  // open: clk, clr

  assign ballX = {5{1'b0}};
  assign ballY = {5{1'b0}};
  assign chipId = {5{1'b0}};
  assign leftBatY = Joystick;
endmodule

module test (
  input  [4:0] joyStick,
  input  clock,
  output [31:0] pattern
);

  wire and_1_out, and_2_out, comparator_1_eq, comparator_1_gt, comparator_1_lt, comparator_2_eq,
       comparator_2_gt, comparator_2_lt, comparator_3_eq, comparator_4_eq, nand_1_out, nand_2_out, not_1_out,
       not_2_out, or_1_out, or_2_out, or_3_out, or_4_out, or_5_out, or_6_out;
  wire [31:0] multiplexer_1_out, multiplexer_2_out, shifter_1_out, shifter_2_out;

  Comparator #(.width(5), .mode("unsigned")) comparator_1 (
    .a(5'b00001), .b(joyStick), .gt(comparator_1_gt), .eq(comparator_1_eq), .lt(comparator_1_lt));
  not not_1 (not_1_out, comparator_2_eq);
  Comparator #(.width(5), .mode("unsigned")) comparator_2 (
    .a(joyStick), .b(5'b10000), .gt(comparator_2_gt), .eq(comparator_2_eq), .lt(comparator_2_lt));
  or or_1 (or_1_out, comparator_1_gt, comparator_1_eq);
  Shifter #(.width(32), .shift("rl")) shifter_1 (.in(pattern), .\dist (5'b00001), .out(shifter_1_out));
  Shifter #(.width(32), .shift("rr")) shifter_2 (.in(pattern), .\dist (5'b00001), .out(shifter_2_out));
  Multiplexer #(.width(32)) multiplexer_1 (
    .in0(shifter_2_out), .in1(shifter_1_out), .out(multiplexer_1_out), .sel(or_1_out));  // open: en
  or or_2 (or_2_out, comparator_1_eq, comparator_1_lt);
  or or_3 (or_3_out, comparator_1_eq, comparator_1_lt);
  Multiplexer #(.width(32)) multiplexer_2 (
    .in0(multiplexer_1_out), .in1(32'h38000), .out(multiplexer_2_out), .sel(and_2_out));  // open: en
  and and_1 (and_1_out, or_4_out, not_1_out, or_6_out);
  and and_2 (and_2_out, or_3_out, not_2_out);
  not not_2 (not_2_out, or_5_out);
  or or_4 (or_4_out, comparator_2_gt, nand_1_out);
  nand nand_1 (nand_1_out, or_2_out, comparator_4_eq);
  Register #(.width(32)) register_1 (.D(multiplexer_2_out), .en(and_1_out), .Q(pattern), .clk(clock));  // open: clr
  Comparator #(.width(32), .mode("unsigned")) comparator_3 (
    .a(pattern), .b(32'h7), .eq(comparator_3_eq));  // open: gt, lt
  Comparator #(.width(32), .mode("unsigned")) comparator_4 (
    .a(32'he0000000), .b(pattern), .eq(comparator_4_eq));  // open: gt, lt
  or or_5 (or_5_out, pattern[31], pattern[30], pattern[29], pattern[28], pattern[27], pattern[26], pattern[25], pattern[24], pattern[23], pattern[22], pattern[21], pattern[20], pattern[19], pattern[18], pattern[17], pattern[16], pattern[15], pattern[14], pattern[13], pattern[12], pattern[11], pattern[10], pattern[9], pattern[8], pattern[7], pattern[6], pattern[5], pattern[4], pattern[3], pattern[2], pattern[1], pattern[0]);
  nand nand_2 (nand_2_out, comparator_3_eq, comparator_1_lt);
  or or_6 (or_6_out, nand_2_out, comparator_2_lt);
endmodule

module inc (
  input  [4:0] X,
  output [4:0] R,
  output Cout
);

  wire [4:1] and_1_out;

  assign {Cout, and_1_out} = {and_1_out, 1'b1} & X;  // AND_Gate and_1, 5 bits wide
  assign R = X ^ {and_1_out, 1'b1};  // XOR_Gate xor_1, 5 bits wide
endmodule

module ballVideo (
  input  [4:0] in,
  output [31:0] out
);

  Shifter #(.width(32), .shift("rl")) shifter_1 (.in(32'h1), .\dist (in), .out(out));
endmodule

module chip (
  input  [4:0] in_1,
  output [31:0] out_2
);

  wire comparator_1_eq;
  wire [4:0] subtractor_1_out;
  wire [31:0] shifter_1_out, shifter_2_out;

  Comparator #(.width(5), .mode("unsigned")) comparator_1 (
    .a(in_1), .b(5'b11110), .eq(comparator_1_eq));  // open: gt, lt
  Shifter #(.width(32)) shifter_1 (.in(32'h7), .\dist (in_1), .out(shifter_1_out));
  Subtractor #(.width(5)) subtractor_1 (.a(in_1), .b(5'b00001), .out(subtractor_1_out));  // open: bin, bout
  Shifter #(.width(32)) shifter_2 (.in(32'h7), .\dist (subtractor_1_out), .out(shifter_2_out));
  Multiplexer #(.width(32)) multiplexer_1 (
    .in0(shifter_1_out), .in1(shifter_2_out), .out(out_2), .sel(comparator_1_eq));  // open: en
endmodule
